// Logisim project CompactALUext.circ as structural Verilog: 10 circuits, main circuit ALU
module ALU (
  input  [3:0] ALU_Control,
  input  [7:0] Bus_A,
  input  [7:0] Bus_B,
  output [7:0] ALUoutput,
  output Equal
);

  wire not_2_out, not_3_out, not_4_out, not_6_out, not_7_out, not_8_out, not_9_out;
  wire [7:0] multiplex_1_out_4, multiplexer_2_out, negator_1_out, not_1_out, subtractor_1_out;

  Negator negator_1 (.in(Bus_A), .out(negator_1_out));
  Multiplex multiplex_1 (
    .in_1(Bus_A), .in_2(Bus_B), .in_3(ALU_Control[2:0]), .out_4(multiplex_1_out_4));  // open: Unsigned_Overflow, Signed_Overflow
  assign not_1_out = ~Bus_A;  // NOT_Gate not_1, 8 bits wide
  not not_2 (not_2_out, subtractor_1_out[0]);
  not not_3 (not_3_out, subtractor_1_out[1]);
  not not_4 (not_4_out, subtractor_1_out[2]);
  // NOT_Gate not_5 has open pins: in=subtractor_1_out[3], out=open
  not not_6 (not_6_out, subtractor_1_out[4]);
  Subtractor subtractor_1 (.a(Bus_A), .b(Bus_B), .out(subtractor_1_out));  // open: bin, bout
  not not_7 (not_7_out, subtractor_1_out[5]);
  not not_8 (not_8_out, subtractor_1_out[6]);
  not not_9 (not_9_out, subtractor_1_out[7]);
  Multiplexer #(.width(8), .enable("false")) multiplexer_1 (
    .in0(multiplex_1_out_4), .in1(multiplexer_2_out), .out(ALUoutput), .sel(ALU_Control[3]));
  Multiplexer #(.select(3), .width(8), .enable("false")) multiplexer_2 (
    .in0(Bus_A), .in1(Bus_A), .in2(Bus_A), .in3(not_1_out), .in4(negator_1_out), .in5(Bus_A), .in6(Bus_A),
    .in7(Bus_A), .out(multiplexer_2_out), .sel(ALU_Control[2:0]));
  and and_1 (Equal, not_2_out, not_3_out, not_4_out, not_6_out, not_7_out, not_8_out, not_9_out);

  // Notes on the sheet:
  //   11 - Bitwise NOT
  //   12 - Negate
  //   Equality
  //   Our extended ALU adds functionality for:
  //   8,9,10 - mxd, msx, msd - makes sure the data is passed straight through
  //   Extended ALU functionality for NOT and negate
  //   equality test
endmodule

module Multiplex (
  input  [7:0] in_1,
  input  [7:0] in_2,
  input  [2:0] in_3,
  output [7:0] out_4,
  output Unsigned_Overflow,
  output Signed_Overflow
);

  wire add_1_signed_overflow, add_1_unsigned_overflow, and_1_out, and_2_out, not_1_out, not_2_out, not_3_out,
       not_4_out, not_5_out, sub_1_out_4;
  wire [7:0] add_1_out_3, bitand_1_out_3, bitor_1_out_3, shiftleftlogical_1_out_3,
       shiftrightarithmetic_1_out_3, shiftrightlogical_1_out_3, signedlessthan_1_out_3, sub_1_out_3;

  Add add_1 (
    .in_1(in_1), .in_2(in_2), .out_3(add_1_out_3), .Signed_Overflow(add_1_signed_overflow),
    .Unsigned_Overflow(add_1_unsigned_overflow));
  Sub sub_1 (.in_1(in_1), .in_2(in_2), .out_3(sub_1_out_3), .out_4(sub_1_out_4));
  BitOr bitor_1 (.in_1(in_1), .in_2(in_2), .out_3(bitor_1_out_3));
  BitAnd bitand_1 (.in_1(in_1), .in_2(in_2), .out_3(bitand_1_out_3));
  ShiftLeftLogical shiftleftlogical_1 (.in_1(in_1), .in_2(in_2), .out_3(shiftleftlogical_1_out_3));
  SignedLessThan signedlessthan_1 (.in_1(in_1), .in_2(in_2), .out_3(signedlessthan_1_out_3));
  ShiftRightLogical shiftrightlogical_1 (.in_1(in_1), .in_2(in_2), .out_3(shiftrightlogical_1_out_3));
  ShiftRightArithmetic shiftrightarithmetic_1 (.in_1(in_1), .in_2(in_2), .out_3(shiftrightarithmetic_1_out_3));
  not not_1 (not_1_out, in_3[0]);
  not not_2 (not_2_out, in_3[1]);
  not not_3 (not_3_out, in_3[2]);
  not not_4 (not_4_out, in_3[1]);
  not not_5 (not_5_out, in_3[2]);
  assign Unsigned_Overflow = and_1_out ? add_1_unsigned_overflow : 1'bz;  // Controlled_Buffer controlled_buffer_1
  assign Signed_Overflow = and_2_out ? sub_1_out_4 : 1'bz;  // Controlled_Buffer controlled_buffer_2
  assign Signed_Overflow = and_1_out ? add_1_signed_overflow : 1'bz;  // Controlled_Buffer controlled_buffer_3
  and and_1 (and_1_out, not_1_out, not_2_out, not_3_out);
  and and_2 (and_2_out, in_3[0], not_4_out, not_5_out);
  Multiplexer #(.select(3), .width(8)) multiplexer_1 (
    .in0(add_1_out_3), .in1(sub_1_out_3), .in2(bitor_1_out_3), .in3(bitand_1_out_3),
    .in4(shiftleftlogical_1_out_3), .in5(signedlessthan_1_out_3), .in6(shiftrightlogical_1_out_3),
    .in7(shiftrightarithmetic_1_out_3), .out(out_4), .sel(in_3));  // open: en
endmodule

module BitOr (
  input  [7:0] in_1,
  input  [7:0] in_2,
  output [7:0] out_3
);

  assign out_3 = in_1 | in_2;  // OR_Gate or_1, 8 bits wide
endmodule

module BitAnd (
  input  [7:0] in_1,
  input  [7:0] in_2,
  output [7:0] out_3
);

  assign out_3 = in_1 & in_2;  // AND_Gate and_1, 8 bits wide
endmodule

module ShiftLeftLogical (
  input  [7:0] in_1,
  input  [7:0] in_2,
  output [7:0] out_3
);

  Shifter shifter_1 (.in(in_1), .\dist (in_2[2:0]), .out(out_3));
endmodule

module ShiftRightLogical (
  input  [7:0] in_1,
  input  [7:0] in_2,
  output [7:0] out_3
);

  Shifter #(.shift("lr")) shifter_1 (.in(in_1), .\dist (in_2[2:0]), .out(out_3));
endmodule

module ShiftRightArithmetic (
  input  [7:0] in_1,
  input  [7:0] in_2,
  output [7:0] out_3
);

  Shifter #(.shift("ar")) shifter_1 (.in(in_1), .\dist (in_2[2:0]), .out(out_3));
endmodule

module SignedLessThan (
  input  [7:0] in_1,
  input  [7:0] in_2,
  output [7:0] out_3
);

  wire comparator_1_lt;

  Comparator comparator_1 (.a(in_1), .b(in_2), .lt(comparator_1_lt));  // open: gt, eq
  assign out_3 = {{7{1'b0}}, comparator_1_lt};  // Bit_Extender bit_extender_1
endmodule

module Add (
  input  [7:0] in_1,
  input  [7:0] in_2,
  output [7:0] out_3,
  output Signed_Overflow,
  output Unsigned_Overflow
);

  wire adder_1_cout;

  Adder #(.width(7)) adder_1 (.a(in_1[6:0]), .b(in_2[6:0]), .out(out_3[6:0]), .cin(1'b0), .cout(adder_1_cout));
  Adder #(.width(1)) adder_2 (.a(in_1[7]), .b(in_2[7]), .out(out_3[7]), .cin(adder_1_cout), .cout(Signed_Overflow));
  xor xor_1 (Unsigned_Overflow, Signed_Overflow, adder_1_cout);
endmodule

module Sub (
  input  [7:0] in_1,
  input  [7:0] in_2,
  output [7:0] out_3,
  output out_4
);

  wire [7:0] negator_1_out;

  Add add_1 (.in_1(in_1), .in_2(negator_1_out), .out_3(out_3), .Signed_Overflow(out_4));  // open: Unsigned_Overflow
  Negator negator_1 (.in(in_2), .out(negator_1_out));
endmodule
