// Logisim project cpu.circ as structural Verilog: 19 circuits, main circuit register
module main (
);

  wire alusrc, and_1_out, beq, clock, disp, equal, jr, luicontrol, lw, not_1_out, regwriteenable, sw;
  wire [1:0] regbusa, regbusb, regwrite;
  wire [3:0] alucontrol, displaylogic_1_out_5, displaylogic_1_out_6, displaylogic_1_out_7,
       displaylogic_1_out_8, displaylogic_1_out_9, displaylogic_1_out_10, displaylogic_1_out_11,
       displaylogic_1_out_12;
  wire [7:0] adder_1_out, alu_1_aluoutput, controlled_buffer_1_out, imm, multiplexer_1_out,
       multiplexer_2_out, multiplexer_3_out, multiplexer_4_out, multiplexer_5_out, offset, regfileinput,
       register_1_q, register_2_bus_a, register_2_bus_b, rom_1_data;

  Multiplexer #(.width(8)) multiplexer_1 (
    .in0(adder_1_out), .in1(regfileinput), .out(multiplexer_1_out), .sel(jr));  // open: en
  Adder adder_1 (.a(multiplexer_2_out), .b(register_1_q), .out(adder_1_out));  // open: cin, cout
  Multiplexer #(.width(8)) multiplexer_2 (
    .in0(8'h1), .in1(offset), .out(multiplexer_2_out), .sel(and_1_out));  // open: en
  Register register_1 (.D(multiplexer_1_out), .Q(register_1_q), .clk(clock));  // open: en, clr
  Clock clock_1 (.out(clock));
  and and_1 (and_1_out, beq, equal);
  ROM rom_1 (.addr(register_1_q), .data(rom_1_data));  // open: sel
  control control_1 (
    .Instruction(rom_1_data), .enabled(regwriteenable), .W(regwrite), .A(regbusa), .B(regbusb),
    .ALU(alucontrol), .Lui(luicontrol), .ALU_Source(alusrc), .Disp(disp), .Lw(lw), .Sw(sw), .Jr(jr), .Beq(beq));
  extend extend (.Instruction(rom_1_data), .out_2(imm));
  offset u_offset (.Instruction(rom_1_data), .out_2(offset));
  register register_2 (
    .Bus_W(regfileinput), .Clock(clock), .RegWriteEnable(regwriteenable), .RW(regwrite), .RA(regbusa),
    .RB(regbusb), .Bus_A(register_2_bus_a), .Bus_B(register_2_bus_b));
  Multiplexer #(.width(8)) multiplexer_3 (
    .in0(register_2_bus_b), .in1(imm), .out(multiplexer_3_out), .sel(alusrc));  // open: en
  Hex_Digit_Display hex_digit_display_1 (.value(displaylogic_1_out_5));  // open: dp
  Multiplexer #(.width(8)) multiplexer_4 (
    .in0(register_2_bus_a), .in1(imm), .out(multiplexer_4_out), .sel(luicontrol));  // open: en
  Multiplexer #(.width(8)) multiplexer_5 (
    .in0(multiplexer_3_out), .in1(8'h4), .out(multiplexer_5_out), .sel(luicontrol));  // open: en
  Hex_Digit_Display hex_digit_display_2 (.value(displaylogic_1_out_6));  // open: dp
  assign controlled_buffer_1_out = sw ? register_2_bus_b : 8'bz;  // Controlled_Buffer controlled_buffer_1
  Hex_Digit_Display hex_digit_display_3 (.value(displaylogic_1_out_7));  // open: dp
  ALU alu_1 (
    .Bus_A(multiplexer_4_out), .Bus_B(multiplexer_5_out), .ALU_Control(alucontrol), .Equal(equal),
    .ALUoutput(alu_1_aluoutput));
  Hex_Digit_Display hex_digit_display_4 (.value(displaylogic_1_out_8));  // open: dp
  Hex_Digit_Display hex_digit_display_5 (.value(displaylogic_1_out_9));  // open: dp
  Hex_Digit_Display hex_digit_display_6 (.value(displaylogic_1_out_10));  // open: dp
  displaylogic displaylogic_1 (
    .r0(regfileinput), .imm(imm), .out_5(displaylogic_1_out_5), .out_6(displaylogic_1_out_6),
    .out_7(displaylogic_1_out_7), .out_8(displaylogic_1_out_8), .out_9(displaylogic_1_out_9),
    .out_10(displaylogic_1_out_10), .out_11(displaylogic_1_out_11), .out_12(displaylogic_1_out_12),
    .display_control(disp), .clock(clock));
  Hex_Digit_Display hex_digit_display_7 (.value(displaylogic_1_out_11));  // open: dp
  Multiplexer #(.width(8)) multiplexer_6 (
    .in0(alu_1_aluoutput), .in1(controlled_buffer_1_out), .out(regfileinput), .sel(lw));  // open: en
  RAM ram_1 (.addr(alu_1_aluoutput), .data(controlled_buffer_1_out), .clk(clock), .ld(not_1_out));  // open: sel, clr
  not not_1 (not_1_out, sw);
  Hex_Digit_Display hex_digit_display_8 (.value(displaylogic_1_out_12));  // open: dp
  // Probe on {displaylogic_1_out_5, displaylogic_1_out_6, displaylogic_1_out_7, displaylogic_1_out_8, displaylogic_1_out_9, displaylogic_1_out_10, displaylogic_1_out_11, displaylogic_1_out_12}

  // Notes on the sheet:
  //   15 is bit xor
  //   14 is set on greater than zero (pointless)
  //   contents of rom_1 (hex, n*v repeats v):
  //   6e 8 20
endmodule

module register (
  input  RegWriteEnable,
  input  [1:0] RW,
  input  [1:0] RA,
  input  [1:0] RB,
  input  [7:0] Bus_W,
  input  Clock,
  output [7:0] Bus_A,
  output [7:0] Bus_B
);

  wire [7:0] controlled_buffer_1_out, demultiplexer_1_out0, demultiplexer_1_out1, demultiplexer_1_out2,
       demultiplexer_1_out3, r0_q, r1_q, rd_q, rs_q;

  Demultiplexer #(.select(2), .width(8), .tristate("true")) demultiplexer_1 (
    .out0(demultiplexer_1_out0), .out1(demultiplexer_1_out1), .out2(demultiplexer_1_out2),
    .out3(demultiplexer_1_out3), .in(controlled_buffer_1_out), .sel(RW));  // open: en
  assign controlled_buffer_1_out = RegWriteEnable ? Bus_W : 8'bz;  // Controlled_Buffer controlled_buffer_1
  Register r0 (.D(demultiplexer_1_out0), .Q(r0_q), .clk(Clock));  // open: en, clr
  Register r1 (.D(demultiplexer_1_out1), .Q(r1_q), .clk(Clock));  // open: en, clr
  Register rs (.D(demultiplexer_1_out2), .Q(rs_q), .clk(Clock));  // open: en, clr
  Register rd (.D(demultiplexer_1_out3), .Q(rd_q), .clk(Clock));  // open: en, clr
  Multiplexer #(.select(2), .width(8)) multiplexer_1 (
    .in0(r0_q), .in1(r1_q), .in2(rs_q), .in3(rd_q), .out(Bus_A), .sel(RA));  // open: en
  Multiplexer #(.select(2), .width(8)) multiplexer_2 (
    .in0(r0_q), .in1(r1_q), .in2(rs_q), .in3(rd_q), .out(Bus_B), .sel(RB));  // open: en
endmodule

module control (
  input  [7:0] Instruction,
  output enabled,
  output [1:0] W,
  output [1:0] A,
  output [1:0] B,
  output [3:0] ALU,
  output Lui,
  output ALU_Source,
  output Disp,
  output Lw,
  output Sw,
  output Jr,
  output Beq
);

  controlregwriteenabled controlregwriteenabled_1 (.Instruction(Instruction), .regwriteenabled(enabled));
  controlrw controlrw_1 (.Instruction(Instruction), .controlrw(W));
  controlra controlra_1 (.Instruction(Instruction), .control_ra(A));
  controlrb controlrb_1 (.Instruction(Instruction), .controlrb(B));
  controlALU controlalu_1 (.Instruction(Instruction), .controlALU(ALU));
  controllui controllui_1 (.Instruction(Instruction), .controllui(Lui));
  controlALUsrc controlalusrc_1 (.Instruction(Instruction), .controlALUsrc(ALU_Source));
  controldisp controldisp_1 (.Instruction(Instruction), .controldisp(Disp));
  controllw controllw_1 (.Instruction(Instruction), .controllw(Lw));
  controlsw controlsw_1 (.Instruction(Instruction), .controlsw(Sw));
  controljr controljr_1 (.Instruction(Instruction), .controljr(Jr));
  controlbeq controlbeq_1 (.Instruction(Instruction), .controlbeq(Beq));
endmodule

// CRWE
module controlregwriteenabled (
  input  [7:0] Instruction,
  output regwriteenabled
);

  wire beq_out, disp_out, jr_check_out, jump_out, not_1_out, not_2_out, not_3_out, not_4_out, not_5_out,
       not_6_out, not_7_out, not_8_out, sw_out;

  not not_1 (not_1_out, Instruction[6]);
  not not_2 (not_2_out, Instruction[7]);
  not not_3 (not_3_out, Instruction[6]);
  not not_4 (not_4_out, Instruction[5]);
  not not_5 (not_5_out, Instruction[1]);
  not not_6 (not_6_out, Instruction[7]);
  not not_7 (not_7_out, Instruction[5]);
  not not_8 (not_8_out, Instruction[6]);
  and jr_check (jr_check_out, Instruction[0], not_5_out, Instruction[2], Instruction[3], not_6_out, not_7_out, not_8_out);
  and disp (disp_out, Instruction[5], not_1_out, not_2_out);
  and sw (sw_out, Instruction[5], not_3_out, Instruction[7]);
  and jump (jump_out, not_4_out, Instruction[6], Instruction[7]);
  and beq (beq_out, Instruction[5], Instruction[6], Instruction[7]);
  nor nor_1 (regwriteenabled, jr_check_out, disp_out, sw_out, jump_out, beq_out);
endmodule

// CRW
module controlrw (
  input  [7:0] Instruction,
  output [1:0] controlrw
);

  wire msd_out, msx_out, mxd_out, not_1_out, not_2_out, not_3_out, not_4_out, not_5_out, not_6_out,
       not_7_out, not_8_out, not_9_out, not_10_out, not_11_out, not_12_out, not_13_out, not_14_out,
       not_15_out, not_16_out, or_1_out;
  wire [1:0] multiplexer_1_out;

  not not_1 (not_1_out, Instruction[0]);
  not not_2 (not_2_out, Instruction[1]);
  not not_3 (not_3_out, Instruction[2]);
  not not_4 (not_4_out, Instruction[5]);
  not not_5 (not_5_out, Instruction[6]);
  not not_6 (not_6_out, Instruction[7]);
  not not_7 (not_7_out, Instruction[1]);
  not not_8 (not_8_out, Instruction[2]);
  not not_9 (not_9_out, Instruction[5]);
  not not_10 (not_10_out, Instruction[6]);
  not not_11 (not_11_out, Instruction[7]);
  not not_12 (not_12_out, Instruction[0]);
  not not_13 (not_13_out, Instruction[2]);
  not not_14 (not_14_out, Instruction[5]);
  not not_15 (not_15_out, Instruction[6]);
  not not_16 (not_16_out, Instruction[7]);
  and mxd (mxd_out, not_1_out, not_2_out, not_3_out, Instruction[3], not_6_out, not_4_out, not_5_out);
  and msx (msx_out, Instruction[0], not_7_out, not_8_out, Instruction[3], not_11_out, not_9_out, not_10_out);
  and msd (msd_out, not_12_out, Instruction[1], not_13_out, Instruction[3], not_16_out, not_14_out, not_15_out);
  Multiplexer #(.width(2)) multiplexer_1 (
    .in0(2'b11), .in1({1'b0, Instruction[4]}), .out(multiplexer_1_out), .sel(mxd_out));  // open: en
  Multiplexer #(.width(2)) multiplexer_2 (
    .in0(multiplexer_1_out), .in1(2'b10), .out(controlrw), .sel(or_1_out));  // open: en
  or or_1 (or_1_out, msx_out, msd_out);
endmodule

// CRA
module controlra (
  input  [7:0] Instruction,
  output [1:0] control_ra
);

  wire beq_out, disp_out, jr_out, lw_out, msd_out, msx_out, mxd_out, neg_out, not_1_out, not_2_out,
       not_4_out, not_5_out, not_6_out, not_7_out, not_8_out, not_9_out, not_10_out, not_11_out, not_12_out,
       not_13_out, not_14_out, not_15_out, not_16_out, not_17_out, not_18_out, not_19_out, not_20_out,
       not_21_out, not_22_out, not_23_out, not_24_out, not_25_out, not_26_out, not_27_out, not_28_out,
       not_29_out, not_30_out, not_31_out, not_32_out, not_33_out, or_out, rd_out, rx_out, sw_out;
  wire [1:0] multiplexer_1_out, multiplexer_2_out;

  not not_1 (not_1_out, Instruction[0]);
  not not_2 (not_2_out, Instruction[1]);
  // NOT_Gate not_3 has open pins: in=Instruction[2], out=open
  not not_4 (not_4_out, Instruction[5]);
  not not_5 (not_5_out, Instruction[6]);
  not not_6 (not_6_out, Instruction[7]);
  not not_7 (not_7_out, Instruction[1]);
  not not_8 (not_8_out, Instruction[2]);
  not not_9 (not_9_out, Instruction[5]);
  not not_10 (not_10_out, Instruction[6]);
  not not_11 (not_11_out, Instruction[7]);
  not not_12 (not_12_out, Instruction[0]);
  not not_13 (not_13_out, Instruction[2]);
  not not_14 (not_14_out, Instruction[5]);
  not not_15 (not_15_out, Instruction[6]);
  not not_16 (not_16_out, Instruction[7]);
  not not_17 (not_17_out, Instruction[2]);
  not not_18 (not_18_out, Instruction[5]);
  not not_19 (not_19_out, Instruction[6]);
  not not_20 (not_20_out, Instruction[7]);
  not not_21 (not_21_out, Instruction[0]);
  not not_22 (not_22_out, Instruction[1]);
  not not_23 (not_23_out, Instruction[5]);
  not not_24 (not_24_out, Instruction[6]);
  not not_25 (not_25_out, Instruction[7]);
  not not_26 (not_26_out, Instruction[6]);
  not not_27 (not_27_out, Instruction[7]);
  not not_28 (not_28_out, Instruction[7]);
  not not_29 (not_29_out, Instruction[6]);
  not not_30 (not_30_out, Instruction[7]);
  not not_31 (not_31_out, Instruction[6]);
  and mxd (mxd_out, not_1_out, not_2_out, Instruction[3], not_4_out, not_5_out, not_6_out);
  and msx (msx_out, Instruction[0], not_7_out, not_8_out, Instruction[3], not_9_out, not_10_out, not_11_out);
  and msd (msd_out, not_12_out, Instruction[1], not_13_out, Instruction[3], not_14_out, not_15_out, not_16_out);
  and not_32 (not_32_out, Instruction[0], Instruction[1], not_17_out, Instruction[3], not_18_out, not_19_out, not_20_out);
  and neg (neg_out, not_21_out, not_22_out, Instruction[2], Instruction[3], not_23_out, not_24_out, not_25_out);
  and disp (disp_out, Instruction[5], not_26_out, not_27_out);
  and \or  (or_out, Instruction[5], Instruction[6], not_28_out);
  and lw (lw_out, Instruction[5], not_29_out, not_30_out);
  and sw (sw_out, Instruction[5], not_31_out, Instruction[7]);
  and beq (beq_out, Instruction[5], Instruction[6], Instruction[7]);
  not not_33 (not_33_out, Instruction[1]);
  or rd (rd_out, mxd_out, msd_out);
  and jr (jr_out, Instruction[0], not_33_out, Instruction[2], Instruction[3]);
  Multiplexer #(.width(2)) multiplexer_1 (.in0(2'b10), .in1(2'b11), .out(multiplexer_1_out), .sel(rd_out));  // open: en
  or rx (rx_out, msx_out, not_32_out, neg_out, disp_out, or_out, lw_out, sw_out, jr_out);
  Multiplexer #(.width(2)) multiplexer_2 (
    .in0(multiplexer_1_out), .in1({1'b0, Instruction[4]}), .out(multiplexer_2_out), .sel(rx_out));  // open: en
  Multiplexer #(.width(2)) multiplexer_3 (
    .in0(multiplexer_2_out), .in1(2'b00), .out(control_ra), .sel(beq_out));  // open: en
endmodule

// CRB
module controlrb (
  input  [7:0] Instruction,
  output [1:0] controlrb
);

  wire and_1_out;

  and and_1 (and_1_out, Instruction[5], Instruction[6], Instruction[7]);
  Multiplexer #(.width(2)) multiplexer_1 (
    .in0({1'b0, Instruction[4]}), .in1(2'b01), .out(controlrb), .sel(and_1_out));  // open: en
endmodule

// CALU
module controlALU (
  input  [7:0] Instruction,
  output [3:0] controlALU
);

  wire or_1_out;
  wire [3:0] multiplexer_2_out;

  or or_1 (or_1_out, Instruction[5], Instruction[6], Instruction[7]);
  Multiplexer #(.width(4)) multiplexer_1 (
    .in0(Instruction[3:0]), .in1(multiplexer_2_out), .out(controlALU), .sel(or_1_out));  // open: en
  Multiplexer #(.select(3), .width(4)) multiplexer_2 (
    .in0(4'b0000), .in1(4'b1000), .in2(4'b0100), .in3(4'b0010), .in4(4'b0000), .in5(4'b0000), .in6(4'b0010),
    .in7(4'b0000), .out(multiplexer_2_out), .sel(Instruction[7:5]));  // open: en
endmodule

// CLUI
module controllui (
  input  [7:0] Instruction,
  output controllui
);

  wire not_1_out, not_2_out;

  not not_1 (not_1_out, Instruction[5]);
  not not_2 (not_2_out, Instruction[7]);
  and _010 (controllui, not_1_out, Instruction[6], not_2_out);
endmodule

// CSW
module controlsw (
  input  [7:0] Instruction,
  output controlsw
);

  wire not_1_out;

  not not_1 (not_1_out, Instruction[6]);
  and _101 (controlsw, Instruction[5], not_1_out, Instruction[7]);
endmodule

// CDISP
module controldisp (
  input  [7:0] Instruction,
  output controldisp
);

  wire not_1_out, not_2_out;

  not not_1 (not_1_out, Instruction[6]);
  and _001 (controldisp, Instruction[5], not_1_out, not_2_out);
  not not_2 (not_2_out, Instruction[7]);
endmodule

// CLW
module controllw (
  input  [7:0] Instruction,
  output controllw
);

  wire not_1_out, not_2_out;

  not not_1 (not_1_out, Instruction[5]);
  not not_2 (not_2_out, Instruction[6]);
  and _100 (controllw, not_1_out, not_2_out, Instruction[7]);
endmodule

// CJR
module controljr (
  input  [7:0] Instruction,
  output controljr
);

  wire not_1_out, not_2_out, not_3_out, not_4_out;

  not not_1 (not_1_out, Instruction[1]);
  not not_2 (not_2_out, Instruction[5]);
  not not_3 (not_3_out, Instruction[6]);
  not not_4 (not_4_out, Instruction[7]);
  and _00001101 (controljr, Instruction[0], not_1_out, Instruction[2], Instruction[3], not_2_out, not_3_out, not_4_out);
endmodule

// CALUSRC
module controlALUsrc (
  input  [7:0] Instruction,
  output controlALUsrc
);

  Multiplexer #(.select(3)) multiplexer_1 (
    .in0(1'b0), .in1(1'b1), .in2(1'b1), .in3(1'b1), .in4(1'b1), .in5(1'b1), .in7(1'b0), .out(controlALUsrc),
    .sel(Instruction[7:5]));  // open: in6, en
endmodule

// CBEQ
module controlbeq (
  input  [7:0] Instruction,
  output controlbeq
);

  and _111 (controlbeq, Instruction[5], Instruction[6], Instruction[7]);
endmodule

module extend (
  input  [7:0] Instruction,
  output [7:0] out_2
);


  assign out_2 = {4'b0000, Instruction[3:0]};
endmodule

module displaylogic (
  input  [7:0] r0,
  input  [7:0] imm,
  input  display_control,
  input  clock,
  output [3:0] out_5,
  output [3:0] out_6,
  output [3:0] out_7,
  output [3:0] out_8,
  output [3:0] out_9,
  output [3:0] out_10,
  output [3:0] out_11,
  output [3:0] out_12
);

  wire [3:0] controlled_buffer_1_out;
  wire [7:0] demultiplexer_1_out0, demultiplexer_1_out1, demultiplexer_1_out2, demultiplexer_1_out3;

  Demultiplexer #(.select(4), .width(8)) demultiplexer_1 (
    .out0(demultiplexer_1_out0), .out1(demultiplexer_1_out1), .out2(demultiplexer_1_out2),
    .out3(demultiplexer_1_out3), .in(r0), .sel(controlled_buffer_1_out));  // open: out4, out5, out6, out7, out8, out9, out10, out11, out12, out13, out14, out15, en
  assign controlled_buffer_1_out = display_control ? imm[3:0] : 4'bz;  // Controlled_Buffer controlled_buffer_1
  Register register_1 (.D(demultiplexer_1_out0), .Q({out_11, out_12}), .clk(clock));  // open: en, clr
  Register register_2 (.D(demultiplexer_1_out1), .Q({out_9, out_10}), .clk(clock));  // open: en, clr
  Register register_3 (.D(demultiplexer_1_out2), .Q({out_7, out_8}), .clk(clock));  // open: en, clr
  Register register_4 (.D(demultiplexer_1_out3), .Q({out_5, out_6}), .clk(clock));  // open: en, clr

  // Notes on the sheet:
  //   3
  //   2
  //   1
  //   0
endmodule

module displogic2 (
  input  [7:0] r0,
  input  [7:0] r1,
  input  [7:0] imm,
  input  display_control,
  input  clock,
  output [3:0] out_6,
  output [3:0] out_7,
  output [3:0] out_8,
  output [3:0] out_9,
  output [3:0] out_10,
  output [3:0] out_11,
  output [3:0] out_12,
  output [3:0] out_13
);

  wire [3:0] controlled_buffer_1_out;
  wire [7:0] demultiplexer_1_out0, demultiplexer_1_out1, demultiplexer_1_out2, demultiplexer_1_out3,
       multiplexer_1_out;

  Multiplexer #(.width(8)) multiplexer_1 (.in0(r0), .in1(r1), .out(multiplexer_1_out), .sel(imm[4]));  // open: en
  Demultiplexer #(.select(4), .width(8)) demultiplexer_1 (
    .out0(demultiplexer_1_out0), .out1(demultiplexer_1_out1), .out2(demultiplexer_1_out2),
    .out3(demultiplexer_1_out3), .in(multiplexer_1_out), .sel(controlled_buffer_1_out));  // open: out4, out5, out6, out7, out8, out9, out10, out11, out12, out13, out14, out15, en
  assign controlled_buffer_1_out = display_control ? imm[3:0] : 4'bz;  // Controlled_Buffer controlled_buffer_1
  Register register_1 (.D(demultiplexer_1_out0), .Q({out_12, out_13}), .clk(clock));  // open: en, clr
  Register register_2 (.D(demultiplexer_1_out1), .Q({out_10, out_11}), .clk(clock));  // open: en, clr
  Register register_3 (.D(demultiplexer_1_out2), .Q({out_8, out_9}), .clk(clock));  // open: en, clr
  Register register_4 (.D(demultiplexer_1_out3), .Q({out_6, out_7}), .clk(clock));  // open: en, clr

  // Notes on the sheet:
  //   3
  //   2
  //   1
  //   0
endmodule

module offset (
  input  [7:0] Instruction,
  output [7:0] out_2
);


  assign out_2 = {{4{Instruction[4]}}, Instruction[3:0]};
endmodule
